// Logisim project Denis_4BitALU.circ as structural Verilog: 5 circuits, main circuit 4-Bit ALU
module _4_Bit_ALU (
  input  A3,
  input  A2,
  input  A1,
  input  A0,
  input  B3,
  input  B2,
  input  B1,
  input  B0,
  input  S2,
  input  S1,
  input  S0,
  output OF,
  output R3,
  output R2,
  output R1,
  output R0
);

  wire [3:0] interface_1_r, undriven, undriven_2;

  Hex_Digit_Display hex_digit_display_1 (.value(undriven), .dp(1'b0));
  Hex_Digit_Display hex_digit_display_2 (.value(undriven_2), .dp(1'b0));
  Interface interface_1 (
    .A3(A3), .R3(R3), .A2(A2), .R2(R2), .A1(A1), .R1(R1), .A0(A0), .R0(R0), .B3(B3), .B2(B2), .B1(B1),
    .B0(B0), .S2(S2), .S1(S1), .S0(S0), .R(interface_1_r), .OF(OF));
  Hex_Digit_Display hex_digit_display_3 (.value(interface_1_r), .dp(1'b0));

  // Notes on the sheet:
  //   Kleinprojekt Arithmetic and Logic Unit
  //   Teamname:
  //   ausgeführt von
  //   vorname.name@students.fhnw.ch
  //   vorname.name@students.fhnw.ch
  //   vorname.name@students.fhnw.ch
  //   vorname.name@students.fhnw.ch
  //   Mephisto
endmodule

module Interface (
  input  A0,
  input  A1,
  input  A2,
  input  A3,
  input  B0,
  input  B1,
  input  B2,
  input  B3,
  input  S0,
  input  S1,
  input  S2,
  output [3:0] R,
  output R0,
  output R1,
  output R2,
  output R3,
  output OF
);
endmodule

module Halbadierer (
  input  A,
  input  B,
  output S,
  output C
);

  xor xor_1 (S, A, B);
  and and_1 (C, A, B);
endmodule

module Volladierer (
  input  C,
  input  A,
  input  B,
  output S,
  output C_2
);

  wire Halbaddierer_c, Halbaddierer_s, halbadierer_1_c;

  Halbadierer Halbaddierer (.A(A), .B(B), .S(Halbaddierer_s), .C(Halbaddierer_c));
  Halbadierer halbadierer_1 (.A(C), .B(Halbaddierer_s), .S(S), .C(halbadierer_1_c));
  or or_1 (C_2, halbadierer_1_c, Halbaddierer_c);
endmodule

module _4Bitaddierer (
  input  A0,
  input  A1,
  input  A2,
  input  A3,
  input  B0,
  input  B1,
  input  B2,
  input  B3,
  output R0,
  output R1,
  output R2,
  output R3,
  output C
);

  wire halbadierer_1_c, volladierer_1_c_2, volladierer_2_c_2;

  Halbadierer halbadierer_1 (.A(A0), .B(B0), .S(R0), .C(halbadierer_1_c));
  Volladierer volladierer_1 (.C(halbadierer_1_c), .A(A1), .B(B1), .S(R1), .C_2(volladierer_1_c_2));
  Volladierer volladierer_2 (.C(volladierer_1_c_2), .A(A2), .B(B2), .S(R2), .C_2(volladierer_2_c_2));
  Volladierer volladierer_3 (.C(volladierer_2_c_2), .A(A3), .B(B3), .S(R3), .C_2(C));
endmodule
