// Logisim project Muffin Soldiers 4BitALU.circ as structural Verilog
module _4_Bit_ALU (
  input  A3,
  input  A2,
  input  A1,
  input  A0,
  input  B3,
  input  B2,
  input  B1,
  input  B0,
  input  S2,
  input  S1,
  input  S0,
  output OF,
  output R3,
  output R2,
  output R1,
  output R0
);

  wire [3:0] interface_1_r, undriven, undriven_2;

  Hex_Digit_Display hex_digit_display_1 (.value(undriven), .dp(1'b0));
  Hex_Digit_Display hex_digit_display_2 (.value(undriven_2), .dp(1'b0));
  Interface interface_1 (
    .A3(A3), .R3(R3), .A2(A2), .R2(R2), .A1(A1), .R1(R1), .A0(A0), .R0(R0), .B3(B3), .B2(B2), .B1(B1),
    .B0(B0), .S2(S2), .S1(S1), .S0(S0), .R(interface_1_r), .OF(OF));
  Hex_Digit_Display hex_digit_display_3 (.value(interface_1_r), .dp(1'b0));

  // Notes on the sheet:
  //   Kleinprojekt Arithmetic and Logic Unit
  //   Teamname:
  //   ausgeführt von
  //   thomas.wilde@students.fhnw.ch
  //   denis.augsburger@students.fhnw.ch
  //   nicolas.mauchle@students.fhnw.ch
  //   piero.steinger@students.fhnw.ch
  //   Muffin Soldiers
endmodule

module Interface (
  input  A0,
  input  A1,
  input  A2,
  input  A3,
  input  B0,
  input  B1,
  input  B2,
  input  B3,
  input  S0,
  input  S1,
  input  S2,
  output [3:0] R,
  output R0,
  output R1,
  output R2,
  output R3,
  output OF
);

  wire [3:0] and_1_r0, not_1_r0, not_2_r0, or_1_r0;
  wire [4:0] n4bitaddierer_1_r0, n4bitsubtrahierer_1_r0, times2_1_r0, times4_1_r0;

  OR or_1 (
    .A0(A0), .A1(A1), .A2(A2), .A3(A3), .B0(B0), .B1(B1), .B2(B2), .B3(B3), .R0(or_1_r0[0]), .R1(or_1_r0[1]),
    .R2(or_1_r0[2]), .R3(or_1_r0[3]));
  AND and_1 (
    .A0(A0), .A1(A1), .A2(A2), .A3(A3), .B0(B0), .B1(B1), .B2(B2), .B3(B3), .R0(and_1_r0[0]),
    .R1(and_1_r0[1]), .R2(and_1_r0[2]), .R3(and_1_r0[3]));
  \not  not_1 (
    .A0(A0), .A1(A1), .A2(A2), .A3(A3), .R0(not_1_r0[0]), .R1(not_1_r0[1]), .R2(not_1_r0[2]), .R3(not_1_r0[3]));
  \not  not_2 (
    .A0(B0), .A1(B1), .A2(B2), .A3(B3), .R0(not_2_r0[0]), .R1(not_2_r0[1]), .R2(not_2_r0[2]), .R3(not_2_r0[3]));
  _4Bitaddierer u_4bitaddierer_1 (
    .A0(A0), .A1(A1), .A2(A2), .A3(A3), .B0(B0), .B1(B1), .B2(B2), .B3(B3), .R0(n4bitaddierer_1_r0[0]),
    .R1(n4bitaddierer_1_r0[1]), .R2(n4bitaddierer_1_r0[2]), .R3(n4bitaddierer_1_r0[3]),
    .C(n4bitaddierer_1_r0[4]));
  _4Bitsubtrahierer u_4bitsubtrahierer_1 (
    .A0(A0), .A1(A1), .A2(A2), .A3(A3), .B0(B0), .B1(B1), .B2(B2), .B3(B3), .R0(n4bitsubtrahierer_1_r0[0]),
    .R1(n4bitsubtrahierer_1_r0[1]), .R2(n4bitsubtrahierer_1_r0[2]), .R3(n4bitsubtrahierer_1_r0[3]),
    .C(n4bitsubtrahierer_1_r0[4]));
  times2 times2_1 (
    .A0(A0), .A1(A1), .A2(A2), .A3(A3), .R0(times2_1_r0[0]), .R1(times2_1_r0[1]), .R2(times2_1_r0[2]),
    .R3(times2_1_r0[3]), .C(times2_1_r0[4]));
  times4 times4_1 (
    .A0(A0), .A1(A1), .A2(A2), .A3(A3), .R0(times4_1_r0[0]), .R1(times4_1_r0[1]), .R2(times4_1_r0[2]),
    .R3(times4_1_r0[3]), .C(times4_1_r0[4]));
  Multiplexer #(.select(3), .width(5), .enable("false")) multiplexer_1 (
    .in0({1'b0, or_1_r0}), .in1({1'b0, and_1_r0}), .in2({1'b0, not_1_r0}), .in3({1'b0, not_2_r0}),
    .in4(n4bitaddierer_1_r0), .in5(n4bitsubtrahierer_1_r0), .in6(times2_1_r0), .in7(times4_1_r0),
    .out({OF, R}), .sel({S2, S1, S0}));

  assign R0 = R[0];
  assign R1 = R[1];
  assign R2 = R[2];
  assign R3 = R[3];

  // Notes on the sheet:
  //   S = 0 -> A or B
  //   S = 1 -> A and B
  //   S = 2 -> not A
  //   S = 3 -> not B
  //   S = 4 -> A plus B
  //   S = 5 -> A minus B
  //   S = 6 -> A times2
  //   S = 7 -> A times4
endmodule

module Halbadierer (
  input  A,
  input  B,
  output S,
  output C
);

  xor xor_1 (S, A, B);
  and and_1 (C, A, B);
endmodule

module Volladierer (
  input  C,
  input  A,
  input  B,
  output S,
  output C_2
);

  wire Halbaddierer_c, Halbaddierer_s, halbadierer_1_c;

  Halbadierer Halbaddierer (.A(A), .B(B), .S(Halbaddierer_s), .C(Halbaddierer_c));
  Halbadierer halbadierer_1 (.A(C), .B(Halbaddierer_s), .S(S), .C(halbadierer_1_c));
  or or_1 (C_2, halbadierer_1_c, Halbaddierer_c);
endmodule

module _4Bitaddierer (
  input  A0,
  input  A1,
  input  A2,
  input  A3,
  input  B0,
  input  B1,
  input  B2,
  input  B3,
  output R0,
  output R1,
  output R2,
  output R3,
  output C
);

  wire volladierer_1_c_2, volladierer_2_c_2, volladierer_3_c_2;

  Volladierer volladierer_1 (.C(1'b0), .A(A0), .B(B0), .S(R0), .C_2(volladierer_1_c_2));
  Volladierer volladierer_2 (.C(volladierer_1_c_2), .A(A1), .B(B1), .S(R1), .C_2(volladierer_2_c_2));
  Volladierer volladierer_3 (.C(volladierer_2_c_2), .A(A2), .B(B2), .S(R2), .C_2(volladierer_3_c_2));
  Volladierer volladierer_4 (.C(volladierer_3_c_2), .A(A3), .B(B3), .S(R3), .C_2(C));
endmodule

module times2 (
  input  A0,
  input  A1,
  input  A2,
  input  A3,
  output R0,
  output R1,
  output R2,
  output R3,
  output C
);

  _4Bitaddierer u_4bitaddierer_1 (
    .A0(A0), .A1(A1), .A2(A2), .A3(A3), .B0(A0), .B1(A1), .B2(A2), .B3(A3), .R0(R0), .R1(R1), .R2(R2),
    .R3(R3), .C(C));
endmodule

module times4 (
  input  A0,
  input  A1,
  input  A2,
  input  A3,
  output R0,
  output R1,
  output R2,
  output R3,
  output C
);

  wire times2_1_c, times2_1_r1, times2_1_r2, times2_1_r3, times2_2_c, times2_2_r3;

  times2 times2_1 (
    .A0(A0), .A1(A1), .A2(A2), .A3(A3), .R0(R0), .R1(times2_1_r1), .R2(times2_1_r2), .R3(times2_1_r3),
    .C(times2_1_c));
  times2 times2_2 (
    .A0(times2_1_r1), .A1(times2_1_r2), .A2(times2_1_r3), .A3(times2_1_c), .R0(R1), .R1(R2), .R2(R3),
    .R3(times2_2_r3), .C(times2_2_c));
  or or_1 (C, times2_2_r3, times2_2_c);
endmodule

module AND (
  input  A0,
  input  A1,
  input  A2,
  input  A3,
  input  B0,
  input  B1,
  input  B2,
  input  B3,
  output R0,
  output R1,
  output R2,
  output R3
);

  and and_1 (R0, A0, B0);
  and and_2 (R1, A1, B1);
  and and_3 (R2, A2, B2);
  and and_4 (R3, A3, B3);
endmodule

module OR (
  input  A0,
  input  A1,
  input  A2,
  input  A3,
  input  B0,
  input  B1,
  input  B2,
  input  B3,
  output R0,
  output R1,
  output R2,
  output R3
);

  or or_1 (R0, A0, B0);
  or or_2 (R1, A1, B1);
  or or_3 (R2, A2, B2);
  or or_4 (R3, A3, B3);
endmodule

module \not  (
  input  A0,
  input  A1,
  input  A2,
  input  A3,
  output R0,
  output R1,
  output R2,
  output R3
);

  not not_1 (R0, A0);
  not not_2 (R1, A1);
  not not_3 (R2, A2);
  not not_4 (R3, A3);
endmodule

module _4Bitsubtrahierer (
  input  A0,
  input  A1,
  input  A2,
  input  A3,
  input  B0,
  input  B1,
  input  B2,
  input  B3,
  output R0,
  output R1,
  output R2,
  output R3,
  output C
);

  wire not_1_out, not_2_out, not_3_out, not_4_out, not_5_out, volladierer_1_c_2, volladierer_2_c_2,
       volladierer_3_c_2, volladierer_4_c_2;

  not not_1 (not_1_out, 1'b0);
  not not_2 (not_2_out, B0);
  not not_3 (not_3_out, B1);
  not not_4 (not_4_out, B2);
  not not_5 (not_5_out, B3);
  Volladierer volladierer_1 (.C(not_1_out), .A(A0), .B(not_2_out), .S(R0), .C_2(volladierer_1_c_2));
  Volladierer volladierer_2 (.C(volladierer_1_c_2), .A(A1), .B(not_3_out), .S(R1), .C_2(volladierer_2_c_2));
  Volladierer volladierer_3 (.C(volladierer_2_c_2), .A(A2), .B(not_4_out), .S(R2), .C_2(volladierer_3_c_2));
  Volladierer volladierer_4 (.C(volladierer_3_c_2), .A(A3), .B(not_5_out), .S(R3), .C_2(volladierer_4_c_2));
  not not_6 (C, volladierer_4_c_2);
endmodule
