// Logisim project Nicolas_Mauchle_4BitALU.circ as structural Verilog: 4 circuits, main circuit 4-Bit ALU
module _4_Bit_ALU (
  input  A3,
  input  A2,
  input  A1,
  input  A0,
  input  B3,
  input  B2,
  input  B1,
  input  B0,
  input  S2,
  input  S1,
  input  S0,
  output OF,
  output R3,
  output R2,
  output R1,
  output R0
);

  wire [3:0] interface_1_r, undriven, undriven_2;

  Hex_Digit_Display hex_digit_display_1 (.value(undriven), .dp(1'b0));
  Hex_Digit_Display hex_digit_display_2 (.value(undriven_2), .dp(1'b0));
  Interface interface_1 (
    .A3(A3), .R3(R3), .A2(A2), .R2(R2), .A1(A1), .R1(R1), .A0(A0), .R0(R0), .B3(B3), .B2(B2), .B1(B1),
    .B0(B0), .S2(S2), .S1(S1), .S0(S0), .R(interface_1_r), .OF(OF));
  Hex_Digit_Display hex_digit_display_3 (.value(interface_1_r), .dp(1'b0));

  // Notes on the sheet:
  //   Kleinprojekt Arithmetic and Logic Unit
  //   Teamname:
  //   ausgeführt von
  //   vorname.name@students.fhnw.ch
  //   vorname.name@students.fhnw.ch
  //   vorname.name@students.fhnw.ch
  //   vorname.name@students.fhnw.ch
  //   Mephisto
endmodule

module Interface (
  input  A0,
  input  A1,
  input  A2,
  input  A3,
  input  B0,
  input  B1,
  input  B2,
  input  B3,
  input  S0,
  input  S1,
  input  S2,
  output [3:0] R,
  output R0,
  output R1,
  output R2,
  output R3,
  output OF
);

  NOT_A not_a_1 (.A0(A0), .A1(A1), .A2(A2), .A3(A3));  // open: R0, R1, R2, R3
  NOT_B not_b_1 (.B0(B0), .B1(B1), .B2(B2), .B3(B3));  // open: R0, R1, R2, R3
endmodule

module NOT_A (
  input  A0,
  input  A1,
  input  A2,
  input  A3,
  output R0,
  output R1,
  output R2,
  output R3
);

  not not_1 (R0, A0);
  not not_2 (R1, A1);
  not not_3 (R2, A2);
  not not_4 (R3, A3);
endmodule

module NOT_B (
  input  B0,
  input  B1,
  input  B2,
  input  B3,
  output R0,
  output R1,
  output R2,
  output R3
);

  not not_1 (R0, B0);
  not not_2 (R1, B1);
  not not_3 (R2, B2);
  not not_4 (R3, B3);
endmodule
